# Fritzing sketch scheme (saved by Fritzing 0.9.6b)

parts:
  U1 = Module 4 Relais 5V [package="Module 4 Relais 5V"]
  Raspberry_Pi_1 = Raspberry Pi B+
  L1 = Solenoid
  HLK-PM1 = HLK-PM12 [part_number=HLK-PM12]
  LED2 = smd LED [color="Infrared (940nm)" package="0603 [SMD]"]
  S1 = Pushbutton [package=THT]
  RHT1 = Humidity and Temperature Sensor RHT03

nets:
  VCC: U1.VCC, Raspberry_Pi_1.3v3
  GND: U1.GND, Raspberry_Pi_1.GND, S1.leg1, RHT1.GND_1
  N1: U1.IN1, Raspberry_Pi_1.GPIO17
  N2: U1.IN2, U1.IN3, Raspberry_Pi_1.GPIO27
  N3: U1.IN4, Raspberry_Pi_1.GPIO22
  N4: U1.K1-NF, U1.K4-NF, HLK-PM1.+Vo
  N5: U1.K2-NF, L1.pin1
  N6: U1.K3-NF, L1.pin2
  N7: U1.K1-Com, U1.K2-Com, U1.K3-NO
  N8: U1.K3-Com, U1.K2-NO, HLK-PM1.-Vo, LED2.anode
  N9: Raspberry_Pi_1.GPIO4, RHT1.Data-signal
  N10: Raspberry_Pi_1.GPIO16, S1.leg0
  5V: Raspberry_Pi_1.5V, RHT1.Vcc

notes:
  MASTER SWITCH
  IR ILLUMINATOR
  IR LIGHT
  DOOR SWITCH
  Door Actuator 12V
  DHT22 temperature humidity sensor

custom parts:
  Module 4 Relais 5V: Module 4 Relais 5V 4x SPD-06VDC-SD-C
