# Fritzing sketch shema kure (saved by Fritzing 0.9.6b)

parts:
  U1 = Module 4 Relais 5V [package="Module 4 Relais 5V"]
  Raspberry_Pi_1 = Raspberry Pi B+
  L1 = Solenoid  # not connected
  HLK-PM1 = HLK-PM12 [part_number=HLK-PM12]
  LED2 = smd LED [color="Infrared (940nm)" package="0603 [SMD]"]
  S1 = Pushbutton [package=THT]

nets:
  VCC: U1.VCC, Raspberry_Pi_1.3v3
  GND: U1.GND, Raspberry_Pi_1.GND
  N1: U1.IN1, Raspberry_Pi_1.GPIO17
  N2: U1.IN2, U1.IN3, Raspberry_Pi_1.GPIO27
  N3: U1.IN4, Raspberry_Pi_1.GPIO22
  N4: U1.K2-NF, U1.K1-NO, U1.K3-NO
  N5: U1.K3-NF, U1.K2-NO, HLK-PM1.-Vo, LED2.anode
  N6: U1.K1-Com, U1.K4-Com, HLK-PM1.+Vo
  N7: Raspberry_Pi_1.GPIO5, S1.leg0
  N8: Raspberry_Pi_1.5V, S1.leg1

notes:
  MASTER SWITCH
  IR ILLUMINATOR
  IR LIGHT
  DOOR SWITCH

custom parts:
  Module 4 Relais 5V: Module 4 Relais 5V 4x SPD-06VDC-SD-C
